// Logisim project Processador Completo.circ as structural Verilog: 5 circuits, main circuit main
module main (
);

  wire cu_control_unit_1_type_r, sel_r_i;
  wire [1:0] ula_op;
  wire [4:0] multiplexer_1_out, multiplexer_2_out, rd, rs_i, rs_r, rt_i, rt_r;
  wire [5:2] cu_control_unit_1_funct;
  wire [31:0] br_banco_de_registradores_1_br_rs, br_banco_de_registradores_1_br_rt,
       \mi_memória_de_instruções_1_instruction , \ula_unidade_lógica_e_aritmetica_1_data ;

  \MI___Memória_de_Instruções  \mi_memória_de_instruções_1  (.Instruction(\mi_memória_de_instruções_1_instruction ));  // open: clock
  Multiplexer #(.width(5), .enable("false")) multiplexer_1 (
    .in0(rt_r), .in1(rt_i), .out(multiplexer_1_out), .sel(sel_r_i));
  not not_1 (sel_r_i, cu_control_unit_1_type_r);
  Multiplexer #(.width(5), .enable("false")) multiplexer_2 (
    .in0(rs_r), .in1(rs_i), .out(multiplexer_2_out), .sel(sel_r_i));
  BR___Banco_de_Registradores br_banco_de_registradores_1 (
    .RS(multiplexer_2_out), .RT(multiplexer_1_out), .RD(rd), .REG_WRTIE(cu_control_unit_1_type_r),
    .BR_RS(br_banco_de_registradores_1_br_rs), .BR_RT(br_banco_de_registradores_1_br_rt),
    .DATA(\ula_unidade_lógica_e_aritmetica_1_data ));
  CU___Control_Unit cu_control_unit_1 (
    .Instruction(\mi_memória_de_instruções_1_instruction ), .Type_R(cu_control_unit_1_type_r),
    .FUNCT({cu_control_unit_1_funct, ula_op}), .RD_R(rd), .RT_R(rt_r), .RS_R(rs_r), .RT_I(rt_i), .RS_I(rs_i));  // open: SHANT, Imediate, Type_I, Label, Type_J
  \ULA___Unidade_Lógica_e_Aritmetica  \ula_unidade_lógica_e_aritmetica_1  (
    .BR_RS(br_banco_de_registradores_1_br_rs), .BR_RT(br_banco_de_registradores_1_br_rt),
    .DATA(\ula_unidade_lógica_e_aritmetica_1_data ), .ULA_OP(ula_op));
endmodule

module BR___Banco_de_Registradores (
  input  [4:0] RS,
  input  [4:0] RT,
  input  [4:0] RD,
  input  REG_WRTIE,
  input  [31:0] DATA,
  output [31:0] BR_RS,
  output [31:0] BR_RT
);

  wire regdxx;
  wire [31:0] reg1, reg2, reg3, reg4, reg5, reg6, reg7, reg8, reg9, reg10, reg11, reg12, reg13, reg14, reg15,
       reg16, reg17, reg18, reg19, reg20, reg21, reg22, reg23, reg24, reg25, reg26, reg27, reg28, reg29,
       reg30, reg31, reg32;

  Demultiplexer #(.select(5), .enable("false")) demultiplexer_1 (
    .out0(regdxx), .out1(regdxx), .out2(regdxx), .out3(regdxx), .out4(regdxx), .out5(regdxx), .out6(regdxx),
    .out7(regdxx), .out8(regdxx), .out9(regdxx), .out10(regdxx), .out11(regdxx), .out12(regdxx),
    .out13(regdxx), .out14(regdxx), .out15(regdxx), .out16(regdxx), .out17(regdxx), .out18(regdxx),
    .out19(regdxx), .out20(regdxx), .out21(regdxx), .out22(regdxx), .out23(regdxx), .out24(regdxx),
    .out25(regdxx), .out26(regdxx), .out27(regdxx), .out28(regdxx), .out29(regdxx), .out30(regdxx),
    .out31(regdxx), .in(REG_WRTIE), .sel(RD));
  Register #(.width(32), .Select("low")) register_1 (.D(DATA), .en(regdxx), .Q(reg1));  // open: clk, clr
  Register #(.width(32), .Select("low")) register_2 (.D(DATA), .en(regdxx), .Q(reg2));  // open: clk, clr
  Register #(.width(32), .Select("low")) register_3 (.en(regdxx), .Q(reg3));  // open: D, clk, clr
  Register #(.width(32), .Select("low")) register_4 (.D(DATA), .en(regdxx), .Q(reg4));  // open: clk, clr
  Register #(.width(32), .Select("low")) register_5 (.D(DATA), .en(regdxx), .Q(reg5));  // open: clk, clr
  Register #(.width(32), .Select("low")) register_6 (.D(DATA), .en(regdxx), .Q(reg6));  // open: clk, clr
  Register #(.width(32), .Select("low")) register_7 (.D(DATA), .en(regdxx), .Q(reg7));  // open: clk, clr
  Register #(.width(32), .Select("low")) register_8 (.D(DATA), .en(regdxx), .Q(reg8));  // open: clk, clr
  Register #(.width(32), .Select("low")) register_9 (.D(DATA), .en(regdxx), .Q(reg9));  // open: clk, clr
  Register #(.width(32), .Select("low")) register_10 (.D(DATA), .en(regdxx), .Q(reg10));  // open: clk, clr
  Register #(.width(32), .Select("low")) register_11 (.D(DATA), .en(regdxx), .Q(reg11));  // open: clk, clr
  Register #(.width(32), .Select("low")) register_12 (.D(DATA), .en(regdxx), .Q(reg12));  // open: clk, clr
  Register #(.width(32), .Select("low")) register_13 (.D(DATA), .en(regdxx), .Q(reg13));  // open: clk, clr
  Register #(.width(32), .Select("low")) register_14 (.D(DATA), .en(regdxx), .Q(reg14));  // open: clk, clr
  Register #(.width(32), .Select("low")) register_15 (.D(DATA), .en(regdxx), .Q(reg15));  // open: clk, clr
  Register #(.width(32), .Select("low")) register_16 (.D(DATA), .en(regdxx), .Q(reg16));  // open: clk, clr
  Register #(.width(32), .Select("low")) register_17 (.D(DATA), .en(regdxx), .Q(reg17));  // open: clk, clr
  Register #(.width(32), .Select("low")) register_18 (.D(DATA), .en(regdxx), .Q(reg18));  // open: clk, clr
  Register #(.width(32), .Select("low")) register_19 (.D(DATA), .en(regdxx), .Q(reg19));  // open: clk, clr
  Register #(.width(32), .Select("low")) register_20 (.D(DATA), .en(regdxx), .Q(reg20));  // open: clk, clr
  Register #(.width(32), .Select("low")) register_21 (.D(DATA), .en(regdxx), .Q(reg21));  // open: clk, clr
  Register #(.width(32), .Select("low")) register_22 (.D(DATA), .en(regdxx), .Q(reg22));  // open: clk, clr
  Register #(.width(32), .Select("low")) register_23 (.D(DATA), .en(regdxx), .Q(reg23));  // open: clk, clr
  Register #(.width(32), .Select("low")) register_24 (.D(DATA), .en(regdxx), .Q(reg24));  // open: clk, clr
  Register #(.width(32), .Select("low")) register_25 (.D(DATA), .en(regdxx), .Q(reg25));  // open: clk, clr
  Register #(.width(32), .Select("low")) register_26 (.D(DATA), .en(regdxx), .Q(reg26));  // open: clk, clr
  Register #(.width(32), .Select("low")) register_27 (.D(DATA), .en(regdxx), .Q(reg27));  // open: clk, clr
  Register #(.width(32), .Select("low")) register_28 (.D(DATA), .en(regdxx), .Q(reg28));  // open: clk, clr
  Register #(.width(32), .Select("low")) register_29 (.D(DATA), .en(regdxx), .Q(reg29));  // open: clk, clr
  Register #(.width(32), .Select("low")) register_30 (.D(DATA), .en(regdxx), .Q(reg30));  // open: clk, clr
  Register #(.width(32), .Select("low")) register_31 (.D(DATA), .en(regdxx), .Q(reg31));  // open: clk, clr
  Register #(.width(32), .Select("low")) register_32 (.D(DATA), .en(regdxx), .Q(reg32));  // open: clk, clr
  Multiplexer #(.select(5), .width(32), .enable("false")) multiplexer_1 (
    .in0(reg1), .in1(reg2), .in2(reg3), .in3(reg4), .in4(reg5), .in5(reg6), .in6(reg7), .in7(reg8),
    .in8(reg9), .in9(reg10), .in10(reg11), .in11(reg12), .in12(reg13), .in13(reg14), .in14(reg15),
    .in15(reg16), .in16(reg17), .in17(reg18), .in18(reg19), .in19(reg20), .in20(reg21), .in21(reg22),
    .in22(reg23), .in23(reg24), .in24(reg25), .in25(reg26), .in26(reg27), .in27(reg28), .in28(reg29),
    .in29(reg30), .in30(reg31), .in31(reg32), .out(BR_RS), .sel(RS));
  Multiplexer #(.select(5), .width(32), .enable("false")) multiplexer_2 (
    .in0(reg1), .in1(reg2), .in2(reg3), .in3(reg4), .in4(reg5), .in5(reg6), .in6(reg7), .in7(reg8),
    .in8(reg9), .in9(reg10), .in10(reg11), .in11(reg12), .in12(reg13), .in13(reg14), .in14(reg15),
    .in15(reg16), .in16(reg17), .in17(reg18), .in18(reg19), .in19(reg20), .in20(reg21), .in21(reg22),
    .in22(reg23), .in23(reg24), .in24(reg25), .in25(reg26), .in26(reg27), .in27(reg28), .in28(reg29),
    .in29(reg30), .in30(reg31), .in31(reg32), .out(BR_RT), .sel(RT));
endmodule

module \ULA___Unidade_Lógica_e_Aritmetica  (
  input  [31:0] BR_RS,
  input  [1:0] ULA_OP,
  input  [31:0] BR_RT,
  output [31:0] DATA
);

  wire [31:0] adder_1_out, divider_1_out, multiplier_1_out, subtractor_1_out;

  Adder #(.width(32)) adder_1 (.a(BR_RS), .b(BR_RT), .out(adder_1_out));  // open: cin, cout
  Subtractor #(.width(32)) subtractor_1 (.a(BR_RS), .b(BR_RT), .out(subtractor_1_out));  // open: bin, bout
  Multiplier #(.width(32)) multiplier_1 (.a(BR_RS), .b(BR_RT), .out(multiplier_1_out));  // open: cin, cout
  Divider #(.width(32)) divider_1 (.a(BR_RS), .b(BR_RT), .out(divider_1_out));  // open: upper, rem
  Multiplexer #(.select(2), .width(32), .enable("false")) multiplexer_1 (
    .in0(adder_1_out), .in1(subtractor_1_out), .in2(multiplier_1_out), .in3(divider_1_out), .out(DATA),
    .sel(ULA_OP));
endmodule

module \MI___Memória_de_Instruções  (
  input  clock,
  output [31:0] Instruction
);

  wire [23:0] adder_1_out, PC___Programing_Counting_q;

  Adder #(.width(24)) adder_1 (.a(PC___Programing_Counting_q), .b(24'h1), .out(adder_1_out));  // open: cin, cout
  Register #(.width(24), .Select("low")) PC___Programing_Counting (
    .D(adder_1_out), .Q(PC___Programing_Counting_q), .clk(clock));  // open: en, clr
  RAM #(.addrWidth(24), .dataWidth(32), .Select("low")) ram_1 (
    .addr(PC___Programing_Counting_q), .data(Instruction));  // open: sel, clk, ld, clr
endmodule

module CU___Control_Unit (
  input  [31:0] Instruction,
  output Type_R,
  output [5:0] FUNCT,
  output [4:0] SHANT,
  output [4:0] RD_R,
  output [4:0] RT_R,
  output [4:0] RS_R,
  output [15:0] Imediate,
  output [4:0] RT_I,
  output [4:0] RS_I,
  output Type_I,
  output [25:0] Label,
  output Type_J
);

  wire comparator_2_eq, comparator_3_eq, comparator_4_eq, comparator_5_eq, comparator_6_eq, comparator_7_eq;

  Comparator #(.width(6)) comparator_1 (.a(Instruction[31:26]), .b({6{1'b0}}), .eq(Type_R));  // open: gt, lt
  Comparator #(.width(6)) comparator_2 (.a(Instruction[31:26]), .b(6'b100011), .eq(comparator_2_eq));  // open: gt, lt
  Comparator #(.width(6)) comparator_3 (.a(Instruction[31:26]), .b(6'b101011), .eq(comparator_3_eq));  // open: gt, lt
  Comparator #(.width(6)) comparator_4 (.a(Instruction[31:26]), .b(6'b000100), .eq(comparator_4_eq));  // open: gt, lt
  Comparator #(.width(6)) comparator_5 (.a(Instruction[31:26]), .b(6'b001000), .eq(comparator_5_eq));  // open: gt, lt
  Comparator #(.width(6)) comparator_6 (.a(Instruction[31:26]), .b(6'b000010), .eq(comparator_6_eq));  // open: gt, lt
  Comparator #(.width(6)) comparator_7 (.a(Instruction[31:26]), .b(6'b000011), .eq(comparator_7_eq));  // open: gt, lt
  or or_1 (Type_I, comparator_2_eq, comparator_3_eq, comparator_4_eq, comparator_5_eq);
  or or_2 (Type_J, comparator_6_eq, comparator_7_eq);

  assign FUNCT = Instruction[5:0];
  assign Imediate = Instruction[15:0];
  assign Label = Instruction[25:0];
  assign RD_R = Instruction[15:11];
  assign RS_I = Instruction[25:21];
  assign RS_R = Instruction[25:21];
  assign RT_I = Instruction[20:16];
  assign RT_R = Instruction[20:16];
  assign SHANT = Instruction[10:6];

  // Other names for the same wires on the sheet: remained[25:0] = Instruction[25:0]; opcode[5:0] = Instruction[31:26]
endmodule
